# Fritzing sketch levitatingPingPongCircuit (saved by Fritzing 0.9.6b)
breadboards: 1

parts:
  Part1 = Arduino Uno (Rev3)
  Transistor_BD537/BD539 = Basic FET N-Channel [package="TO220 [THT]"]
  Adjustable_power_supply = Power plug
  Resistor = Resistor [tolerance=±5% resistance=2.2k power=0.25W package=THT]
  Fan_motor = DC Motor
  flyback_diode = Rectifier Diode [part_number=1N4001 package="300 mil [THT]"]
  Resistor_2 = Resistor [tolerance=±5% power=0.25W resistance=22k package=THT]
  Capacitor = Electrolytic Capacitor [capacitance=2.2µF voltage=35V package="100 mil [THT, electrolytic]"]
  Sharp_2Y0A21_proximity_sensor = Infrared Proximity Sensor

nets (from the schematic view):
  N1: Part1.A0, Resistor_2.Pin_1, Capacitor.-
  N2: Part1.D9_PWM, Resistor.Pin_1
  5V: Part1.5V, Sharp_2Y0A21_proximity_sensor.Vcc
  GND: Part1.GND, Transistor_BD537/BD539.source, Capacitor.+, Sharp_2Y0A21_proximity_sensor.GND
  N3: Transistor_BD537/BD539.gate, Resistor.Pin_0
  N4: Transistor_BD537/BD539.drain, Fan_motor.pin_1, flyback_diode.anode
  N5: Adjustable_power_supply.VCC, Fan_motor.pin_2, flyback_diode.cathode
  N6: Resistor_2.Pin_0, Sharp_2Y0A21_proximity_sensor.Vout

notes:
  Top power rail is supplied with 5V DC from Arduino Uno. Bottom power rail is supplied with 12V DC from external power upply.
  Note how all GND are connected, which is crucial to making the circuit work.
  RC-Filter (first-order low-pass filter)
  time constant: tau = R * C
  cutoff frequency: omega = 1/RC
